# Fritzing sketch nodemcu-sensor (saved by Fritzing 0.9.3b)
breadboards: 1

parts:
  U1 = NodeMCU V1.0
  S3 = Reed switch [package=THT]
  S2 = Reed switch [package=THT]
  S1 = Reed switch [package=THT]

nets:
  N1: U1.D1, S1.pin_1
  N2: U1.D2, S2.pin_1
  N3: U1.D3, S3.pin_1
  GND: U1.GND, S3.pin_2, S2.pin_2, S1.pin_2

custom parts:
  NodeMCU V1.0: ESP8266 based NodeMCU
